# Fritzing sketch Circuit Sketch v2 (saved by Fritzing 0.9.9b)
breadboards: 1

parts:
  R2 = Resistor [tolerance=±5% power=0.25 resistance=135 package=THT]
  R3 = Resistor [tolerance=±5% power=0.25 resistance=220 package=THT]
  R4 = Resistor [tolerance=±5% power=0.25 resistance=220 package=THT]
  LED1 = LED - 3mm [color="Green (560nm)" current=0.030 package="3 mm [THT]"]
  LED2 = LED - 3mm [color="Green (560nm)" current=0.030 package="3 mm [THT]"]
  LED3 = LED - 3mm [color="Orange (605nm)" current=0.030 package="3 mm [THT]"]
  R5 = Resistor [tolerance=±5% power=0.25 resistance=100 package=THT]
  R6 = Resistor [tolerance=±5% power=0.25 resistance=100 package=THT]
  HC-SR04_Sensor_1 = HC-SR04 Ultrasonic Distance Sensor
  HC-SR04_Sensor_2 = HC-SR04 Ultrasonic Distance Sensor
  HC-SR04_Sensor_3 = HC-SR04 Ultrasonic Distance Sensor
  HC-SR04_Sensor_4 = HC-SR04 Ultrasonic Distance Sensor
  J1 = Piezo Speaker
  J2 = Piezo Speaker
  LED5 = LED - 3mm [color="Red (633nm)" current=0.030 package="3 mm [THT]"]
  LED6 = LED - 3mm [color="Red (633nm)" current=0.030 package="3 mm [THT]"]
  Componente1 = Arduino Yun
  R7 = Photocell (LDR) [package=THT]
  R8 = Resistor [tolerance=±5% power=0.25 resistance=220 package=THT]
  R9 = Photocell (LDR) [package=THT]
  R10 = Resistor [tolerance=±5% power=0.25 resistance=220 package=THT]
  Mod1 = KY-008 Laser Transmitter Module [package="Breakout board"]
  Mod2 = KY-008 Laser Transmitter Module [package="Breakout board"]
  R1 = Resistor [tolerance=±5% power=0.25 resistance=135 package=THT]
  LED7 = LED - 3mm [color="Orange (605nm)" current=0.030 package="3 mm [THT]"]
  LED8 = LED - 3mm [color="Orange (605nm)" current=0.030 package="3 mm [THT]"]
  LED9 = LED - 3mm [color="Orange (605nm)" current=0.030 package="3 mm [THT]"]

nets:
  N1: R2.Pin_0, LED3.anode, LED9.anode
  N2: R2.Pin_1, Componente1.D4
  N3: R3.Pin_0, LED2.anode
  N4: R3.Pin_1, Componente1.D2
  N5: R4.Pin_0, LED1.anode
  N6: R4.Pin_1, Componente1.D3_PWM
  GND: LED1.cathode, LED2.cathode, LED3.cathode, HC-SR04_Sensor_1.GND, HC-SR04_Sensor_2.GND, HC-SR04_Sensor_3.GND, HC-SR04_Sensor_4.GND, J1.pin1, J2.pin1, LED5.cathode, LED6.cathode, Componente1.GND, R7.pin_0, R9.pin_0, Mod1.-, Mod2.-, LED7.cathode, LED8.cathode, LED9.cathode
  N7: R5.Pin_0, J2.pin2, Componente1.D7
  N8: R5.Pin_1, LED5.anode
  N9: R6.Pin_0, J1.pin2, Componente1.D6_PWM
  N10: R6.Pin_1, LED6.anode
  VCC: HC-SR04_Sensor_1.VCC, HC-SR04_Sensor_2.VCC, HC-SR04_Sensor_3.VCC, HC-SR04_Sensor_4.VCC, Componente1.5V, R8.Pin_0, R10.Pin_0, Mod1.S, Mod2.S
  N11: HC-SR04_Sensor_1.TRIG, HC-SR04_Sensor_2.TRIG, HC-SR04_Sensor_3.TRIG, HC-SR04_Sensor_4.TRIG, Componente1.D8
  N12: HC-SR04_Sensor_1.ECHO, Componente1.D9_PWM
  N13: HC-SR04_Sensor_2.ECHO, Componente1.D10_PWM/SS
  N14: HC-SR04_Sensor_3.ECHO, Componente1.D11_PWM/MOSI
  N15: HC-SR04_Sensor_4.ECHO, Componente1.D12/MISO
  N16: Componente1.A0, R7.pin_1, R8.Pin_1
  N17: Componente1.A1, R9.pin_1, R10.Pin_1
  N18: Componente1.D5_PWM, R1.Pin_1
  N19: R1.Pin_0, LED7.anode, LED8.anode

custom parts:
  KY-008 Laser Transmitter Module: KY-008 Laser Transmitter Module, emits a dot shaped red laser beam.
